# Fritzing sketch model4bRFID (saved by Fritzing 0.9.4)
breadboards: 1

parts:
  SERVO1 = Tower Pro SG90 servo [part_number=101246]
  LED1 = smd LED [color="Red (633nm)" package="0603 [SMD]"]
  LED2 = smd LED [color="Red (633nm)" package="0603 [SMD]"]
  Parça1 = RFID-RC522-v2
  R1 = Resistor [tolerance=±5% resistance=220 package="0402 [SMD]"]
  R2 = Resistor [tolerance=±5% resistance=220 package="0402 [SMD]"]
  Raspberry_Pi_2 = Raspberry Pi 4 [part_number=RPI-4-b]
  HC-SR04_Sensor_2 = HC-SR04 Ultrasonic Distance Sensor
  R3 = Resistor [tolerance=±5% resistance=220 package="0402 [SMD]"]
  R4 = Resistor [tolerance=±5% resistance=220 package="0402 [SMD]"]

nets:
  N1: SERVO1.Signal, Raspberry_Pi_2.GPIO17
  +5V: SERVO1.+5V, Raspberry_Pi_2.5V, HC-SR04_Sensor_2.VCC
  GND: SERVO1.GND, LED1.cathode, LED2.cathode, Parça1.GND, Raspberry_Pi_2.GND, HC-SR04_Sensor_2.GND, R3.Pin_0
  N2: LED1.anode, R2.Pin_0
  N3: LED2.anode, R1.Pin_0
  N4: Parça1.SDA, Raspberry_Pi_2.GPIO8
  N5: Parça1.SCK, Raspberry_Pi_2.GPIO11
  N6: Parça1.MOSI, Raspberry_Pi_2.GPIO10
  N7: Parça1.MISO, Raspberry_Pi_2.GPIO9
  N8: Parça1.RST, Raspberry_Pi_2.GPIO25
  3.3V: Parça1.3.3V, Raspberry_Pi_2.3v3
  N9: R1.Pin_1, Raspberry_Pi_2.GPIO27
  N10: R2.Pin_1, Raspberry_Pi_2.GPIO22
  N11: Raspberry_Pi_2.GPIO24, R3.Pin_1, R4.Pin_1
  N12: Raspberry_Pi_2.GPIO23, HC-SR04_Sensor_2.TRIG
  N13: HC-SR04_Sensor_2.ECHO, R4.Pin_0

custom parts:
  Tower Pro SG90 servo: Original file by John De Cristofaro http://www.adafruit.com/products/1449 Adafruit Feedback Servo (Small) Edited by: e-radionica.com 28/9/2015
  RFID-RC522-v2: A simple China made RFID-RC522 Reader; do check the pin labels, as this is a MFRC522 based clone.
  Raspberry Pi 4: The RPi4, a faster version of the awesome Raspberry Pi 2 B ARM Board with 40 pin gpio. Ready for special Raspberry Pi B+ and RPi2 Hat (Hardware attached (on) top)
